// Logisim project cpu.circ as structural Verilog
module CPU (
  input  [15:0] From_Instr_Mem,
  input  clk,
  output [15:0] r0,
  output [15:0] r1,
  output [15:0] r2,
  output [15:0] r3,
  output [15:0] Display_0,
  output [15:0] Display_1,
  output [15:0] Data_Mem_Data,
  output [15:0] To_Instr_Mem,
  output [15:0] Data_Mem_Addr,
  output Data_Mem_Write
);

  wire arithmetic_logic_unit_1_p3, arithmetic_logic_unit_1_p5, instruction_decoder_1_regdest,
       instruction_decoder_1_regwrite, register_file_1_p1, register_file_1_p13;
  wire [1:0] instruction_decoder_1_out_3, instruction_decoder_1_out_4, instruction_decoder_1_out_5,
       multiplexer_1_out;
  wire [15:0] arithmetic_logic_unit_1_p2, arithmetic_logic_unit_1_p4, arithmetic_logic_unit_1_p6,
       data_memory_1_dataout, register_file_1_p14, WriteData;

  Instruction_Decoder instruction_decoder_1 (
    .RegDest(instruction_decoder_1_regdest), .out_3(instruction_decoder_1_out_3),
    .out_4(instruction_decoder_1_out_4), .out_5(instruction_decoder_1_out_5),
    .RegWrite(instruction_decoder_1_regwrite));  // open: in_1, Imm_Addr
  Multiplexer #(.width(2), .enable("false")) multiplexer_1 (
    .in0(instruction_decoder_1_out_4), .in1(instruction_decoder_1_out_5), .out(multiplexer_1_out),
    .sel(instruction_decoder_1_regdest));
  // Register_File register_file_1: pin names not known; wires that end beside it: register_file_1_p1, multiplexer_1_out, instruction_decoder_1_out_5, instruction_decoder_1_out_3, WriteData, instruction_decoder_1_regwrite, register_file_1_p1, r0, r1, clk, r2, r3, register_file_1_p13, register_file_1_p14
  // Arithmetic_Logic_Unit arithmetic_logic_unit_1: pin names not known; wires that end beside it: register_file_1_p13, arithmetic_logic_unit_1_p2, arithmetic_logic_unit_1_p3, arithmetic_logic_unit_1_p4, arithmetic_logic_unit_1_p5, arithmetic_logic_unit_1_p6
  Multiplexer #(.width(16), .enable("false")) multiplexer_2 (
    .in0(register_file_1_p14), .out(arithmetic_logic_unit_1_p2));  // open: in1, sel
  Multiplexer #(.width(16), .enable("false")) multiplexer_3 (
    .in0(data_memory_1_dataout), .in1(arithmetic_logic_unit_1_p4), .out(WriteData),
    .sel(arithmetic_logic_unit_1_p5));
  Data_Memory data_memory_1 (
    .DataIn(arithmetic_logic_unit_1_p4), .Address(arithmetic_logic_unit_1_p6),
    .DataOut(data_memory_1_dataout), .MemWrite(Data_Mem_Write));  // open: Reset

  // Other names for the same wires on the sheet: d0[15:0] = Display_0; d1[15:0] = Display_1;
  //   MemWrite = Data_Mem_Write

  // Notes on the sheet:
  //   This is the current PC that you need to send as OUTPUT
  //   This is the instruction that you would receive as INPUT
  //   rt
  //   This is a CLK that is an INPUT driven from the harness.
  //   Remember, this circuit is loaded from the harness to be tested!
  //   DO NOT CHANGE THE LOCATIONS OF THE INPUTS OR OUTPUTS! IF YOU DO SO, YOU NEED TO MAKE SURE THE PINS ARE IN THE RIGHT PLACES!
  //   RegDest
  //   rd
  //   rs
  //   RegWrite
  //   These are OUTPUTS of the circuit
  //   These are OUTPUTS of the circuit
endmodule

module Data_Memory (
  input  [15:0] DataIn,
  input  [15:0] Address,
  input  Reset,
  input  MemWrite,
  output [15:0] DataOut
);

  wire clk_out, not_1_out;

  Clock clk (.out(clk_out));
  assign DataOut = MemWrite ? DataIn : 16'bz;  // Controlled_Buffer controlled_buffer_1
  RAM #(.addrWidth(16), .dataWidth(16)) ram_1 (
    .addr(Address), .data(DataOut), .sel(1'b1), .clk(clk_out), .ld(not_1_out), .clr(Reset));
  not not_1 (not_1_out, MemWrite);
endmodule

module Instruction_Decoder (
  input  [15:0] in_1,
  output RegDest,
  output [1:0] out_3,
  output [1:0] out_4,
  output [1:0] out_5,
  output RegWrite,
  output Imm_Addr
);

  wire comparator_1_lt, comparator_2_gt, I_RegDest, I_RegWrite, R_RegDest, R_RegWrite;
  wire [1:0] I_rd, I_rs, I_rt, R_rd, R_rs, R_rt;
  wire [3:0] bitselector_1_out;

  R_type_Instruction_Decode r_type_instruction_decode_1 (
    .in_1(in_1), .rd(R_rd), .rt(R_rt), .rs(R_rs), .RegWrite(R_RegWrite), .RegDest(R_RegDest));
  BitSelector #(.width(16), .group(4)) bitselector_1 (.in(in_1), .out(bitselector_1_out), .sel(2'b11));
  Comparator #(.width(4), .mode("unsigned")) comparator_1 (
    .a(4'b0000), .b(bitselector_1_out), .lt(comparator_1_lt));  // open: gt, eq
  Comparator #(.width(4), .mode("unsigned")) comparator_2 (
    .a(bitselector_1_out), .b(4'b0011), .gt(comparator_2_gt));  // open: eq, lt
  I_type_Instruction_Decoder i_type_instruction_decoder_1 (
    .in_1(in_1), .rd(I_rd), .rt(I_rt), .rs(I_rs), .RegWrite(I_RegWrite), .RegDest(I_RegDest));  // open: SignOrUnsign, Imm_Addr

  // Other names for the same wires on the sheet: Instruction_In[15:0] = in_1; rd[1:0] = out_4; rs[1:0] = out_3;
  //   rt[1:0] = out_5

  // Notes on the sheet:
  //   0: write to rd
  //   1: write to rt
endmodule

// R-type decoder
module R_type_Instruction_Decode (
  input  [15:0] in_1,
  output [1:0] rd,
  output [1:0] rt,
  output [1:0] rs,
  output RegWrite,
  output RegDest
);

  BitSelector #(.width(16), .group(2)) bitselector_1 (.in(in_1), .out(rd), .sel(3'b011));
  BitSelector #(.width(16), .group(2)) bitselector_2 (.in(in_1), .out(rt), .sel(3'b100));
  BitSelector #(.width(16), .group(2)) bitselector_3 (.in(in_1), .out(rs), .sel(3'b101));

  assign RegDest = 1'b0;
  assign RegWrite = 1'b1;

  // Notes on the sheet:
  //   (enable write to register)
  //   (select rd as destination register)
endmodule

module I_type_Instruction_Decoder (
  input  [15:0] in_1,
  output [1:0] rd,
  output [1:0] rt,
  output [1:0] rs,
  output SignOrUnsign,
  output RegWrite,
  output RegDest,
  output Imm_Addr
);

  wire addiRW, addiSOU, andiRW, andiSOU, beqRW, beqSOU, bneRW, bneSOU, dispRW, dispSOU, luiRW, luiSOU, lwRW,
       lwSOU, oriRW, oriSOU, swRW, swSOU;
  wire [3:0] InstrSelect;

  beq beq_1 (.Sign(beqSOU), .RegWrite(beqRW));
  ori ori_1 (.Sign(oriSOU), .RegWrite(oriRW));
  lui lui_1 (.Sign(luiSOU), .RegWrite(luiRW));
  BitSelector #(.width(16), .group(4)) bitselector_1 (.in(in_1), .out(InstrSelect), .sel(2'b11));
  BitSelector #(.width(16), .group(2)) bitselector_2 (.in(in_1), .out(rt), .sel(3'b100));
  addi addi_1 (.Sign(addiSOU), .RegWrite(addiRW));
  bne bne_1 (.Sign(bneSOU), .RegWrite(bneRW));
  lw lw_1 (.Sign(lwSOU), .RegWrite(lwRW));
  BitSelector #(.width(16), .group(2)) bitselector_3 (.in(in_1), .out(rs), .sel(3'b101));
  andi andi_1 (.Sign(andiSOU), .RegWrite(andiRW));
  sw sw_1 (.Sign(swSOU), .RegWrite(swRW));
  disp disp_1 (.Sign(dispSOU), .RegWrite(dispRW));
  Multiplexer #(.select(4), .enable("false")) multiplexer_1 (
    .in4(beqSOU), .in5(addiSOU), .in6(andiSOU), .in7(oriSOU), .in8(bneSOU), .in9(swSOU), .in10(luiSOU),
    .in11(lwSOU), .in12(dispSOU), .out(SignOrUnsign), .sel(InstrSelect));  // open: in0, in1, in2, in3, in13, in14, in15
  Multiplexer #(.select(4), .enable("false")) multiplexer_2 (
    .in4(beqRW), .in5(addiRW), .in6(andiRW), .in7(oriRW), .in8(bneRW), .in9(swRW), .in10(luiRW), .in11(lwRW),
    .in12(dispRW), .out(RegWrite), .sel(InstrSelect));  // open: in0, in1, in2, in3, in13, in14, in15

  assign Imm_Addr = 1'b0;
  assign rd = 2'b11;
  assign RegDest = 1'b1;

  // Notes on the sheet:
  //   (rd is not used)
  //   (select rt as destination register)
endmodule

module beq (
  output Sign,
  output RegWrite
);


  assign RegWrite = 1'b0;
  assign Sign = 1'b1;
endmodule

module addi (
  output Sign,
  output RegWrite
);


  assign RegWrite = 1'b1;
  assign Sign = 1'b1;
endmodule

module andi (
  output Sign,
  output RegWrite
);


  assign RegWrite = 1'b1;
  assign Sign = 1'b0;
endmodule

module ori (
  output Sign,
  output RegWrite
);


  assign RegWrite = 1'b1;
  assign Sign = 1'b0;
endmodule

module bne (
  output Sign,
  output RegWrite
);


  assign RegWrite = 1'b0;
  assign Sign = 1'b1;
endmodule

module sw (
  output Sign,
  output RegWrite
);


  assign RegWrite = 1'b0;
  assign Sign = 1'b1;
endmodule

module lui (
  output Sign,
  output RegWrite
);


  assign RegWrite = 1'b1;
  assign Sign = 1'b0;
endmodule

module lw (
  output Sign,
  output RegWrite
);


  assign RegWrite = 1'b1;
  assign Sign = 1'b1;
endmodule

module disp (
  output Sign,
  output RegWrite
);


  assign RegWrite = 1'b0;
  assign Sign = 1'b0;
endmodule
